// Logisim project Project4.circ as structural Verilog: 10 circuits, main circuit main
module main (
  output [31:0] R0
);

  wire ALU_n, ALU_z, clock_1_out, control_1_addzero, control_1_alusrc, control_1_bl, control_1_flagw,
       control_1_memtoreg, control_1_memw, control_1_pcsrc, control_1_regw;
  wire [1:0] control_1_alucode, control_1_regsrc, immsrc;
  wire [3:0] instrsplit_bit3_0, instrsplit_bit15_12, instrsplit_bit19_16, multiplexer_2_out,
       multiplexer_3_out, multiplexer_4_out;
  wire [23:0] instrsplit_bit23_0;
  wire [31:0] adder_1_out, adder_2_out, ALU_output, Data_Memory_out_6, Instruction_Memory_instruction,
       multiplexer_1_out, multiplexer_5_out, multiplexer_6_out, multiplexer_7_out, multiplexer_8_out, PC_q,
       register_file_1_rd1, register_file_1_rd2, signextender_1_out_3;

  Clock clock_1 (.out(clock_1_out));
  Register #(.width(32)) PC (.D(multiplexer_1_out), .Q(PC_q), .clk(clock_1_out));  // open: en, clr
  Multiplexer #(.width(32), .disabled(0), .enable("false")) multiplexer_1 (
    .in0(adder_1_out), .in1(multiplexer_8_out), .out(multiplexer_1_out), .sel(control_1_pcsrc));
  // Probe on immsrc
  Adder #(.width(32)) adder_1 (.a(PC_q), .b(32'h4), .out(adder_1_out), .cin(1'b0));  // open: cout
  Instruction_memory Instruction_Memory (.address_in_pc(PC_q), .instruction(Instruction_Memory_instruction));
  Instrsplitter instrsplit (
    .IW(Instruction_Memory_instruction), .bit19_16(instrsplit_bit19_16), .bit3_0(instrsplit_bit3_0),
    .bit15_12(instrsplit_bit15_12), .bit23_0(instrsplit_bit23_0));
  Adder #(.width(32)) adder_2 (.a(adder_1_out), .b(32'h4), .out(adder_2_out), .cin(1'b0));  // open: cout
  // Probe on Instruction_Memory_instruction
  Multiplexer #(.width(4), .disabled(0), .enable("false")) multiplexer_2 (
    .in0(instrsplit_bit19_16), .in1(4'b1111), .out(multiplexer_2_out), .sel(control_1_regsrc[0]));
  Multiplexer #(.width(4), .disabled(0), .enable("false")) multiplexer_3 (
    .in0(instrsplit_bit3_0), .in1(instrsplit_bit15_12), .out(multiplexer_3_out), .sel(control_1_regsrc[1]));
  Multiplexer #(.width(4), .disabled(0), .enable("false")) multiplexer_4 (
    .in0(instrsplit_bit15_12), .in1(4'b1110), .out(multiplexer_4_out), .sel(control_1_bl));
  signExtender signextender_1 (.bit0_23(instrsplit_bit23_0), .immsrc(immsrc), .out_3(signextender_1_out_3));
  Multiplexer #(.width(32), .disabled(0), .enable("false")) multiplexer_5 (
    .in0(multiplexer_8_out), .in1(adder_1_out), .out(multiplexer_5_out), .sel(control_1_bl));
  Control control_1 (
    .in_1(Instruction_Memory_instruction), .PCsrc(control_1_pcsrc), .memtoReg(control_1_memtoreg),
    .memW(control_1_memw), .ALUsrc(control_1_alusrc), .immsrc(immsrc), .regW(control_1_regw),
    .regsrc(control_1_regsrc), .AddZero(control_1_addzero), .BL(control_1_bl), .flagW(control_1_flagw),
    .ALUcode(control_1_alucode), .Z(ALU_z), .N(ALU_n));  // open: branch
  Multiplexer #(.width(32), .disabled(0), .enable("false")) multiplexer_6 (
    .in0(register_file_1_rd1), .in1({32{1'b0}}), .out(multiplexer_6_out), .sel(control_1_addzero));
  Register_File register_file_1 (
    .Clock(clock_1_out), .A1(multiplexer_2_out), .A2(multiplexer_3_out), .A3(multiplexer_4_out),
    .WE(control_1_regw), .WD3(multiplexer_5_out), .RD1(register_file_1_rd1), .R15(adder_2_out),
    .RD2(register_file_1_rd2), .R0(R0));  // open: Reset
  Multiplexer #(.width(32), .disabled(0), .enable("false")) multiplexer_7 (
    .in0(register_file_1_rd2), .in1(signextender_1_out_3), .out(multiplexer_7_out), .sel(control_1_alusrc));
  ALU ALU (
    .in_1(multiplexer_6_out), .in_2(multiplexer_7_out), .code(control_1_alucode), .N(ALU_n), .Z(ALU_z),
    .\output (ALU_output), .in_4(control_1_flagw));  // open: C
  Data_memory Data_Memory (
    .address(ALU_output), .strword(register_file_1_rd2), .clk(clock_1_out), .we(control_1_memw),
    .out_6(Data_Memory_out_6));  // open: reset, out_7
  Multiplexer #(.width(32), .disabled(0), .enable("false")) multiplexer_8 (
    .in0(ALU_output), .in1(Data_Memory_out_6), .out(multiplexer_8_out), .sel(control_1_memtoreg));
endmodule

module ALU (
  input  [31:0] in_1,
  input  [31:0] in_2,
  input  [1:0] code,
  input  in_4,
  output N,
  output Z,
  output [31:0] \output ,
  output C
);

  wire adder_1_cout, comparator_1_eq, comparator_1_lt, subtractor_1_bout;
  wire [31:0] adder_1_out, and_1_out, or_1_out, subtractor_1_out;

  // Probe on in_1
  // Probe on in_2
  Adder #(.width(32)) adder_1 (.a(in_1), .b(in_2), .out(adder_1_out), .cout(adder_1_cout));  // open: cin
  Subtractor #(.width(32)) subtractor_1 (
    .a(in_1), .b(in_2), .out(subtractor_1_out), .bout(subtractor_1_bout));  // open: bin
  assign and_1_out = in_2 & in_1;  // AND_Gate and_1, 32 bits wide
  assign or_1_out = in_2 | in_1;  // OR_Gate or_1, 32 bits wide
  Multiplexer #(.select(2), .width(32)) multiplexer_1 (
    .in0(adder_1_out), .in1(subtractor_1_out), .in2(and_1_out), .in3(or_1_out), .out(\output ), .sel(code),
    .en(1'b1));
  or or_2 (C, adder_1_cout, subtractor_1_bout);
  Comparator #(.width(32)) comparator_1 (
    .a(\output ), .b({32{1'b0}}), .eq(comparator_1_eq), .lt(comparator_1_lt));  // open: gt
  // Probe on \output 
  Multiplexer #(.disabled(0), .enable("false")) multiplexer_2 (.in0(N), .in1(comparator_1_lt), .out(N), .sel(in_4));
  Multiplexer #(.disabled(0), .enable("false")) multiplexer_3 (.in0(Z), .in1(comparator_1_eq), .out(Z), .sel(in_4));
endmodule

module Instruction_memory (
  input  [31:0] address_in_pc,
  output [31:0] instruction
);

  // Probe on address_in_pc
  ROM #(.dataWidth(32)) rom_1 (.addr(address_in_pc[9:2]), .data(instruction), .sel(1'b1));
  // Probe on instruction

  // Notes on the sheet:
  //   contents of rom_1 (hex, n*v repeats v):
  //   e3a00007 e24dd004 e58de000 e24dd004 e58d4000 e24dd004 e58d0000 e3500002 ba000009 e2400001 ebfffff5
  //   e1a04000 e59d0000 e28dd004 e2400002 e24dd004 e58d0000 ebffffee e0840000 e28dd004 e59d4000 e28dd004
  //   e59de000 e28dd004 e12fff1e
endmodule

module Data_memory (
  input  [31:0] address,
  input  [31:0] strword,
  input  clk,
  input  we,
  input  reset,
  output [31:0] out_6,
  output [31:0] out_7
);

  wire not_1_out;

  not not_1 (not_1_out, we);
  RAM #(.dataWidth(32), .bus("separate")) ram_1 (
    .addr(address[9:2]), .din(strword), .data(out_6), .str(we), .sel(1'b1), .clk(clk), .ld(not_1_out),
    .clr(reset));

  assign out_7 = strword;
endmodule

module Register_File (
  input  Reset,
  input  Clock,
  input  [31:0] WD3,
  input  [3:0] A1,
  input  [31:0] R15,
  input  [3:0] A2,
  input  [3:0] A3,
  input  WE,
  output [31:0] RD1,
  output [31:0] RD2,
  output [31:0] R0
);

  wire decoder_1_out0, decoder_1_out1, decoder_1_out2, decoder_1_out3, decoder_1_out4, decoder_1_out5,
       decoder_1_out6, decoder_1_out7, decoder_1_out8, decoder_1_out9, decoder_1_out10, decoder_1_out11,
       decoder_1_out12, decoder_1_out13, decoder_1_out14;
  wire [31:0] R1_q, R2_q, R3_q, R4_q, R5_q, R6_q, R7_q, R8_q, R9_q, R10_q, R11_q, R12_q, R13_q, R14_q;

  Register #(.width(32)) u_R0 (.D(WD3), .en(decoder_1_out0), .Q(R0), .clk(Clock), .clr(Reset));
  Register #(.width(32)) R1 (.D(WD3), .en(decoder_1_out1), .Q(R1_q), .clk(Clock), .clr(Reset));
  Register #(.width(32)) R2 (.D(WD3), .en(decoder_1_out2), .Q(R2_q), .clk(Clock), .clr(Reset));
  Register #(.width(32)) R3 (.D(WD3), .en(decoder_1_out3), .Q(R3_q), .clk(Clock), .clr(Reset));
  Multiplexer #(.select(4), .width(32), .disabled(0), .enable("false")) multiplexer_1 (
    .in0(R0), .in1(R1_q), .in2(R2_q), .in3(R3_q), .in4(R4_q), .in5(R5_q), .in6(R6_q), .in7(R7_q), .in8(R8_q),
    .in9(R9_q), .in10(R10_q), .in11(R11_q), .in12(R12_q), .in13(R13_q), .in14(R14_q), .in15(R15), .out(RD1),
    .sel(A1));
  Multiplexer #(.select(4), .width(32), .disabled(0), .enable("false")) multiplexer_2 (
    .in0(R0), .in1(R1_q), .in2(R2_q), .in3(R3_q), .in4(R4_q), .in5(R5_q), .in6(R6_q), .in7(R7_q), .in8(R8_q),
    .in9(R9_q), .in10(R10_q), .in11(R11_q), .in12(R12_q), .in13(R13_q), .in14(R14_q), .in15(R15), .out(RD2),
    .sel(A2));
  Register #(.width(32)) R4 (.D(WD3), .en(decoder_1_out4), .Q(R4_q), .clk(Clock), .clr(Reset));
  Register #(.width(32)) R5 (.D(WD3), .en(decoder_1_out5), .Q(R5_q), .clk(Clock), .clr(Reset));
  Register #(.width(32)) R6 (.D(WD3), .en(decoder_1_out6), .Q(R6_q), .clk(Clock), .clr(Reset));
  Register #(.width(32)) R7 (.D(WD3), .en(decoder_1_out7), .Q(R7_q), .clk(Clock), .clr(Reset));
  Decoder #(.select(4), .disabled(0)) decoder_1 (
    .out0(decoder_1_out0), .out1(decoder_1_out1), .out2(decoder_1_out2), .out3(decoder_1_out3),
    .out4(decoder_1_out4), .out5(decoder_1_out5), .out6(decoder_1_out6), .out7(decoder_1_out7),
    .out8(decoder_1_out8), .out9(decoder_1_out9), .out10(decoder_1_out10), .out11(decoder_1_out11),
    .out12(decoder_1_out12), .out13(decoder_1_out13), .out14(decoder_1_out14), .sel(A3), .en(WE));  // open: out15
  Register #(.width(32)) R8 (.D(WD3), .en(decoder_1_out8), .Q(R8_q), .clk(Clock), .clr(Reset));
  Register #(.width(32)) R9 (.D(WD3), .en(decoder_1_out9), .Q(R9_q), .clk(Clock), .clr(Reset));
  Register #(.width(32)) R10 (.D(WD3), .en(decoder_1_out10), .Q(R10_q), .clk(Clock), .clr(Reset));
  Register #(.width(32)) R11 (.D(WD3), .en(decoder_1_out11), .Q(R11_q), .clk(Clock), .clr(Reset));
  Register #(.width(32)) R12 (.D(WD3), .en(decoder_1_out12), .Q(R12_q), .clk(Clock), .clr(Reset));
  Register #(.width(32)) R13 (.D(WD3), .en(decoder_1_out13), .Q(R13_q), .clk(Clock), .clr(Reset));
  Register #(.width(32)) R14 (.D(WD3), .en(decoder_1_out14), .Q(R14_q), .clk(Clock), .clr(Reset));
endmodule

module Control (
  input  [31:0] in_1,
  input  Z,
  input  N,
  output memtoReg,
  output regW,
  output BL,
  output AddZero,
  output memW,
  output PCsrc,
  output branch,
  output ALUsrc,
  output [1:0] immsrc,
  output [1:0] regsrc,
  output [1:0] ALUcode,
  output flagW
);

  wire alu_decoder_1_addzero, alu_decoder_1_nowrite, and_1_out, and_2_out, and_3_out, and_4_out, and_8_out,
       and_9_out, and_10_out, main_decoder_1_aluop, main_decoder_1_branch, main_decoder_1_bx_2,
       main_decoder_1_memw, main_decoder_1_pcsrc, main_decoder_1_regw, or_1_out, or_2_out;

  and and_1 (and_1_out, ~in_1[31], ~in_1[30], ~in_1[29], ~in_1[28]);  // AND_Gate
  and and_2 (and_2_out, in_1[31], in_1[30], in_1[29], ~in_1[28]);  // AND_Gate
  and and_3 (and_3_out, in_1[31], in_1[30], ~in_1[28], ~in_1[28]);  // AND_Gate
  and and_4 (and_4_out, in_1[31], ~in_1[30], in_1[28], in_1[28]);  // AND_Gate
  // Probe on in_1[25:20]
  Main_Decoder main_decoder_1 (
    .op(in_1[27:26]), .BX(in_1[27:4]), .func(in_1[25:20]), .branch(main_decoder_1_branch),
    .PCsrc(main_decoder_1_pcsrc), .memtoReg(memtoReg), .MemW(main_decoder_1_memw), .ALUsrc(ALUsrc),
    .Immsrc(immsrc), .RegW(main_decoder_1_regw), .Regsrc(regsrc), .ALUop(main_decoder_1_aluop),
    .BX_2(main_decoder_1_bx_2), .BL(BL));
  ALU_Decoder alu_decoder_1 (
    .ALUop(main_decoder_1_aluop), .OP(in_1[25:21]), .ALU_control(ALUcode), .FlagW(flagW),
    .AddZero(alu_decoder_1_addzero), .noWrite(alu_decoder_1_nowrite));
  // Probe on in_1[25:21]
  and and_5 (branch, main_decoder_1_branch, or_1_out);
  and and_6 (PCsrc, main_decoder_1_pcsrc, or_1_out);
  and and_7 (memW, main_decoder_1_memw, or_1_out, ~alu_decoder_1_nowrite);  // AND_Gate
  and and_8 (and_8_out, and_4_out, ~Z, N);  // AND_Gate
  and and_9 (and_9_out, ~N, ~Z, and_3_out);  // AND_Gate
  and and_10 (and_10_out, Z, and_1_out);
  and and_11 (regW, or_2_out, or_1_out, ~alu_decoder_1_nowrite);  // AND_Gate
  or or_1 (or_1_out, and_10_out, and_9_out, and_8_out, and_2_out);
  or or_2 (or_2_out, memtoReg, BL, main_decoder_1_regw);
  or or_3 (AddZero, alu_decoder_1_addzero, main_decoder_1_bx_2);
endmodule

module Main_Decoder (
  input  [1:0] op,
  input  [23:0] BX,
  input  [5:0] func,
  output branch,
  output PCsrc,
  output memtoReg,
  output MemW,
  output ALUsrc,
  output [1:0] Immsrc,
  output RegW,
  output [1:0] Regsrc,
  output ALUop,
  output BX_2,
  output BL
);

  wire DP_imm_out, DP_Reg_out, or_4_out;

  Comparator #(.width(24), .mode("unsigned")) comparator_1 (.a(BX), .b(24'h12fff1), .eq(BX_2));  // open: gt, lt
  and DP_Reg (DP_Reg_out, ~op[1], ~op[0], ~BX_2, ~func[5]);  // AND_Gate
  and DP_imm (DP_imm_out, ~op[1], ~op[0], func[5], ~BX_2);  // AND_Gate
  and STR (MemW, ~op[1], op[0], ~func[0], ~BX_2);  // AND_Gate
  and LDR (memtoReg, ~op[1], op[0], func[0], ~BX_2);  // AND_Gate
  and B (branch, op[1], ~op[0], ~BX_2);  // AND_Gate
  or or_1 (PCsrc, branch, BX_2);
  and and_1 (BL, branch, func[4]);
  or or_2 (ALUsrc, DP_imm_out, MemW, memtoReg, branch);
  or or_3 (Immsrc[0], MemW, memtoReg);
  or or_4 (or_4_out, DP_Reg_out, DP_imm_out, DP_imm_out);
  or or_5 (ALUop, DP_Reg_out, DP_imm_out);
  or or_6 (RegW, memtoReg, or_4_out);

  assign Immsrc[1] = branch;
  assign Regsrc = {MemW, branch};
endmodule

module ALU_Decoder (
  input  ALUop,
  input  [4:0] OP,
  output [1:0] ALU_control,
  output FlagW,
  output AddZero,
  output noWrite
);

  wire and_out, or_out, sub_out;

  and sub (sub_out, ALUop, ~OP[0], OP[1], ~OP[2], ~OP[3]);  // AND_Gate
  and \and  (and_out, ALUop, ~OP[0], ~OP[1], ~OP[2], ~OP[3]);  // AND_Gate
  and \or  (or_out, ALUop, OP[0], OP[1], ~OP[2], ~OP[3]);  // AND_Gate
  and mov (AddZero, OP[0], ~OP[1], OP[2], OP[3]);  // AND_Gate
  and cmp (FlagW, ~OP[0], OP[1], ~OP[2], OP[3]);  // AND_Gate
  or or_2 (ALU_control[0], FlagW, sub_out, or_out);
  or or_3 (ALU_control[1], and_out, or_out);

  assign noWrite = FlagW;
endmodule

module signExtender (
  input  [23:0] bit0_23,
  input  [1:0] immsrc,
  output [31:0] out_3
);

  wire [23:0] shifter_1_out;
  wire [31:0] bit_extender_1_out;

  Multiplexer #(.select(2), .width(32), .disabled(0), .enable("false")) multiplexer_1 (
    .in0({{24{1'b0}}, bit0_23[7:0]}), .in1({{20{1'b0}}, bit0_23[11:0]}), .in2(bit_extender_1_out),
    .out(out_3), .sel(immsrc));  // open: in3
  Shifter #(.width(24)) shifter_1 (.in(bit0_23), .\dist (5'b00010), .out(shifter_1_out));
  assign bit_extender_1_out = {{8{shifter_1_out[23]}}, shifter_1_out};  // Bit_Extender bit_extender_1
endmodule

module Instrsplitter (
  input  [31:0] IW,
  output [3:0] bit19_16,
  output [3:0] bit3_0,
  output [3:0] bit15_12,
  output [23:0] bit23_0
);


  assign bit3_0 = IW[3:0];
  assign bit15_12 = IW[15:12];
  assign bit19_16 = IW[19:16];
  assign bit23_0 = IW[23:0];
endmodule
